// Logisim project tlab1.circ as structural Verilog: 1 circuit, main circuit main
module main (
);

  wire multiplexer_1_out, priority_encoder_1_gs, priority_encoder_2_gs, priority_encoder_3_gs, undriven,
       undriven_2, undriven_3, undriven_4, undriven_5, undriven_6, undriven_7, undriven_8, undriven_9,
       undriven_10, undriven_11;
  wire [1:0] priority_encoder_1_out, priority_encoder_2_out;

  Priority_Encoder #(.select(2)) priority_encoder_1 (
    .in0(undriven_4), .in1(undriven_2), .in2(undriven_2), .in3(undriven_2), .out(priority_encoder_1_out),
    .gs(priority_encoder_1_gs));  // open: en_out, en_in
  Priority_Encoder #(.select(2)) priority_encoder_2 (
    .in0(undriven_5), .in1(undriven), .in2(undriven_3), .in3(undriven_6), .out(priority_encoder_2_out),
    .gs(priority_encoder_2_gs));  // open: en_out, en_in
  Multiplexer multiplexer_1 (
    .in0(priority_encoder_1_out[0]), .in1(priority_encoder_2_out[0]), .out(multiplexer_1_out),
    .sel(undriven_9), .en(undriven_10));
  Priority_Encoder #(.select(2)) priority_encoder_3 (
    .in0(priority_encoder_1_gs), .in1(priority_encoder_2_gs), .in2(undriven_7), .in3(undriven_8),
    .gs(priority_encoder_3_gs), .en_out(multiplexer_1_out), .en_in(undriven_11));  // open: out
  // Pins of 1 and 2 bits meet at priority_encoder_1_out
  // Pins of 1 and 2 bits meet at priority_encoder_2_out
endmodule
